// Logisim project 8bit_ALU.circ as structural Verilog: 15 circuits, main circuit main
module main (
  input  [3:0] OpCode,
  input  [7:0] A,
  input  [7:0] B,
  output [7:0] Result,
  output Zero,
  output Equal,
  output LessThan,
  output GreaterThan
);


  // Notes on the sheet:
  //   INPUTS
  //   OPCODES:
  //   0000: ADD
  //   0001: INC
  //   0010: DEC
  //   0011: CMP
  //   0100: NOT
  //   0101: AND
  //   0110: OR
  //   0111: SHR
  //   1000: SHL
  //   1001: XOR
  //   1010: SUB
  //   1011: NAND
  //   1100: NOR
  //   1101: PASS A
  //   8-BIT ALU WITH 14 OPERATIONS
  //   OUTPUTS
endmodule

// ADD
module Adder8bit (
  input  [7:0] A,
  input  [7:0] B,
  output [7:0] Sum,
  output Carry
);

  Adder #(.width(8)) adder_1 ();  // open: a, b, out, cin, cout
endmodule

// INC
module Incrementer8bit (
  input  [7:0] A,
  output [7:0] Result
);

  Adder #(.width(8)) adder_1 ();  // open: a, b, out, cin, cout
endmodule

// DEC
module Decrementer8bit (
  input  [7:0] A,
  output [7:0] Result
);

  Subtractor #(.width(8)) subtractor_1 ();  // open: a, b, out, bin, bout
endmodule

// CMP
module Comparator8bit (
  input  [7:0] A,
  input  [7:0] B,
  output Equal,
  output LessThan,
  output GreaterThan
);

  Comparator #(.width(8)) comparator_1 ();  // open: a, b, gt, eq, lt
endmodule

// NOT
module NOT8bit (
  input  [7:0] A,
  output [7:0] Result
);

  // NOT_Gate not_1 is placed but not wired
endmodule

// AND
module AND8bit (
  input  [7:0] A,
  input  [7:0] B,
  output [7:0] Result
);

  // AND_Gate and_1 is placed but not wired
endmodule

// OR
module OR8bit (
  input  [7:0] A,
  input  [7:0] B,
  output [7:0] Result
);

  // OR_Gate or_1 is placed but not wired
endmodule

// SHR
module ShiftRight8bit (
  input  [7:0] A,
  output [7:0] Result
);

  Shifter #(.width(8), .shift("lr")) shifter_1 ();  // open: in, dist, out
endmodule

// SHL
module ShiftLeft8bit (
  input  [7:0] A,
  output [7:0] Result
);

  Shifter #(.width(8), .shift("ll")) shifter_1 ();  // open: in, dist, out
endmodule

// XOR
module XOR8bit (
  input  [7:0] A,
  input  [7:0] B,
  output [7:0] Result
);

  // XOR_Gate xor_1 is placed but not wired
endmodule

// SUB
module Subtractor8bit (
  input  [7:0] A,
  input  [7:0] B,
  output [7:0] Result,
  output Borrow
);

  Subtractor #(.width(8)) subtractor_1 ();  // open: a, b, out, bin, bout
endmodule

// NAND
module NAND8bit (
  input  [7:0] A,
  input  [7:0] B,
  output [7:0] Result
);

  // NAND_Gate nand_1 is placed but not wired
endmodule

// NOR
module NOR8bit (
  input  [7:0] A,
  input  [7:0] B,
  output [7:0] Result
);

  // NOR_Gate nor_1 is placed but not wired
endmodule

// PASS
module PassA8bit (
  input  [7:0] A,
  output [7:0] Result
);
endmodule
